# Fritzing sketch 2pin-Reed_ON (saved by Fritzing 0.9.3b)
breadboards: 1

parts:
  S1 = Reed switch [package=THT]
  R1 = Resistor [tolerance=±5% resistance=220 package="2010 [SMD]"]
  LED1 = smd LED [color="Red (633nm)" package="1206 [SMD]"]
  Power_plug1 = Power plug

nets:
  N1: S1.pin_1, R1.Pin_1
  N2: S1.pin_2, Power_plug1.VCC
  N3: R1.Pin_0, LED1.anode
  N4: LED1.cathode, Power_plug1.GND

notes:
  LED ON
  Turn on and LED when approaching a magnet to the reed sensor
